# Fritzing sketch picoTracker (saved by Fritzing 0.9.4)

parts:
  Mod1 = Raspberry Pi Pico
  LCD1 = 2.8" SPI TFT Module [part_number=MSP2807]
  Part2 = Adafruit MIDI FeatherWing Kit [part_number=ADA4740]
  Up = Cherry MX Blue
  Down = Cherry MX Blue
  Right = Cherry MX Blue
  Left = Cherry MX Blue
  LT = Cherry MX Blue
  Play = Cherry MX Blue
  RT = Cherry MX Blue
  A = Cherry MX Blue
  B = Cherry MX Blue
  Part1 = Adafruit SDIO microSD Breakout
  U1 = CY-PCM5102 [package="SIP (Single Inline) [THT]"]

nets:
  N1: Mod1.pin_1, Part2.MIDI_RX
  N2: Mod1.pin_2, Part2.MIDI_TX
  GND: Mod1.pin_3, Mod1.pin_13, Mod1.pin_18, Mod1.pin_23, Mod1.pin_38, LCD1.pin2, Part2.GND, Up.pin_2, Down.pin_2, Right.pin_2, Left.pin_2, LT.pin_2, Play.pin_2, RT.pin_2, A.pin_2, B.pin_2, Part1.GND, U1.GND
  N3: Mod1.pin_4, Part1.SCLK
  N4: Mod1.pin_5, Part1.DI
  N5: Mod1.pin_6, Part1.DO
  N6: Mod1.pin_7, Part1.DAT1
  N7: Mod1.pin_9, Part1.DAT2
  N8: Mod1.pin_10, Part1.CS
  N9: Mod1.pin_11, Left.pin_1
  N10: Mod1.pin_12, Down.pin_1
  N11: Mod1.pin_14, Right.pin_1
  N12: Mod1.pin_15, Up.pin_1
  N13: Mod1.pin_16, RT.pin_1
  N14: Mod1.pin_17, B.pin_1
  N15: Mod1.pin_19, A.pin_1
  N16: Mod1.pin_20, LT.pin_1
  N17: Mod1.pin_21, Play.pin_1
  N18: Mod1.pin_22, U1.SCK
  N19: Mod1.pin_24, U1.BCK
  N20: Mod1.pin_25, U1.LCK
  N21: Mod1.pin_26, U1.DIN
  N22: Mod1.pin_27, LCD1.pin5
  N23: Mod1.pin_29, LCD1.pin4
  N24: Mod1.pin_31, LCD1.pin7
  N25: Mod1.pin_32, LCD1.pin6
  N26: Mod1.pin_34, LCD1.pin3
  3.3V: Mod1.pin_36, LCD1.pin1, LCD1.pin8, Part2.3.3V, Part1.3.3V, U1.VIN

custom parts:
  Raspberry Pi Pico: Raspberry Pi Pico. Based around the RP2040 microcontroller the Pico is a low cost microcontroller device bringing Raspberry Pi quality, cost, and easy of use to the microcontroller space. Jan 2021, Split part in to two versions: tht (this one) and SMD. This one will drill holes for a .1 in header in pcb to allow plugging in the module as well as providing pads to solder the module to the top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
  2.8" SPI TFT Module: A generic 2.8 inch LCD TFT 320x240 display with touchscreen and SD card slot. Uses the ILI9341 controller, like the Adafruit displays of this size uses.
  Adafruit MIDI FeatherWing Kit: Turn your Feather into a song-bird with this musically-enabled FeatherWing that adds MIDI input and output jacks to just about any Feather. You get both input and output DIN-5 MIDI jacks, a 3V optically isolator so you can interface with MIDI on 3.3V logic/power microcontrollers, and two blinky indicator LEDs underneath the jacks to help you know when data is sent and received. For those who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
  Cherry MX Blue: Cherry MX Blue Keyswitch button for keyboards
  CY-PCM5102: PCM5102 module
